# Fritzing sketch SparkSofa (saved by Fritzing 0.9.1b)
circuit board: 10.6cm x 5.49999cm
breadboards: 1

parts:
  SS3 = Screw terminal - 4 pins [package=THT]
  OC1 = IC, DIP package, 8 pins [chip_label=IC]
  3_3K = Resistor [tolerance=±5% resistance=220 package=THT]
  SS2 = Screw terminal - 4 pins [package=THT]
  SS1 = Screw terminal - 4 pins [package=THT]
  SM3 = Screw terminal - 4 pins [package=THT]
  SM2 = Screw terminal - 4 pins [package=THT]
  SM1 = Screw terminal - 4 pins [package=THT]
  RELAY1 = RELAY-SOLIDSTATE [package=relay-s108t02]
  3_3K_2 = Resistor [tolerance=±5% resistance=220 package=THT]
  OC2 = IC, DIP package, 8 pins [chip_label=IC]
  3_3K_3 = Resistor [tolerance=±5% resistance=220 package=THT]
  3_3K_4 = Resistor [tolerance=±5% resistance=220 package=THT]
  OC3 = IC, DIP package, 8 pins [chip_label=IC]
  3_3K_5 = Resistor [tolerance=±5% resistance=220 package=THT]
  3_3K_6 = Resistor [tolerance=±5% resistance=220 package=THT]
  D1 = Diode [package=diode-1n4001]
  QR1 = Resistor [tolerance=±5% resistance=220 package=THT]
  RELAY2 = RELAY-SOLIDSTATE [package=relay-s108t02]
  D2 = Diode [package=diode-1n4001]
  QR2 = Resistor [tolerance=±5% resistance=220 package=THT]
  RELAY3 = RELAY-SOLIDSTATE [package=relay-s108t02]
  D3 = Diode [package=diode-1n4001]
  QR3 = Resistor [tolerance=±5% resistance=220 package=THT]
  RELAY4 = RELAY-SOLIDSTATE [package=relay-s108t02]
  D4 = Diode [package=diode-1n4001]
  QR4 = Resistor [tolerance=±5% resistance=220 package=THT]
  RELAY5 = RELAY-SOLIDSTATE [package=relay-s108t02]
  D5 = Diode [package=diode-1n4001]
  QR5 = Resistor [tolerance=±5% resistance=220 package=THT]
  RELAY6 = RELAY-SOLIDSTATE [package=relay-s108t02]
  D6 = Diode [package=diode-1n4001]
  QR6 = Resistor [tolerance=±5% resistance=220 package=THT]
  RELAY7 = RELAY-SOLIDSTATE [package=relay-s108t02]
  D7 = Diode [package=diode-1n4001]
  QR7 = Resistor [tolerance=±5% resistance=220 package=THT]
  C5 = Capacitor Polarized [package=cpol-radial-100uf-25v]
  IC2 = IC, DIP package, 8 pins [chip_label=IC]
  C6 = Capacitor Polarized [package=cpol-radial-10uf-25v]
  10K = Resistor [tolerance=±5% resistance=220 package=THT]
  PE52628NL = PE-52628N [part_number=PE-52628NL]
  J2 = female pin header, 2 pins [form="♀ (female)"]
  10K_2 = Resistor [tolerance=±5% resistance=220 package=THT]
  10K_3 = Resistor [tolerance=±5% resistance=220 package=THT]
  10K_4 = Resistor [tolerance=±5% resistance=220 package=THT]
  10K_5 = Resistor [tolerance=±5% resistance=220 package=THT]
  10K_6 = Resistor [tolerance=±5% resistance=220 package=THT]
  J1 = female pin header, 6 pins [form="♀ (female)"]
  Part1 = Spark Core (v1.0)
  Q1 = NPN-Transistor [package="TO92 [THT]"]
  Q2 = NPN-Transistor [package="TO92 [THT]"]
  Q3 = NPN-Transistor [package="TO92 [THT]"]
  Q4 = NPN-Transistor [package="TO92 [THT]"]
  Q5 = NPN-Transistor [package="TO92 [THT]"]
  Q6 = NPN-Transistor [package="TO92 [THT]"]
  Q7 = NPN-Transistor [package="TO92 [THT]"]
  D8 = Diode [package=diode-1n4001]

nets:
  N1: SS3.pin1, 3_3K_5.Pin_0
  N2: SS3.pin2, SS2.pin2, SS1.pin2, RELAY7.C
  N3: SS3.pin3, 3_3K_6.Pin_0
  N4: SS3.pin4, OC1.pin2, OC1.pin4, OC1.pin5, OC1.pin7, SS2.pin4, SS1.pin4, SM3.pin4, SM2.pin4, SM1.pin4, RELAY1.NO, OC2.pin2, OC2.pin4, OC2.pin5, OC2.pin7, OC3.pin2, OC3.pin4, OC3.pin5, OC3.pin7, RELAY2.NO, RELAY3.NO, RELAY4.NO, RELAY5.NO, RELAY6.NO, RELAY7.NC, C5.-, IC2.pin2, IC2.pin3, IC2.pin4, C6.-, J1.pin3, Part1.GND, Q1.E, Q2.E, Q3.E, Q4.E, Q5.E, Q6.E, Q7.E, D8.A
  N5: OC1.pin1, 3_3K_2.Pin_1
  N6: OC1.pin3, 3_3K.Pin_1
  N7: OC1.pin6, 10K_2.Pin_1, Part1.D3
  N8: OC1.pin8, 10K.Pin_1, Part1.D2
  N9: 3_3K.Pin_0, SS1.pin1
  N10: SS2.pin1, 3_3K_3.Pin_0
  N11: SS2.pin3, 3_3K_4.Pin_0
  N12: SS1.pin3, 3_3K_2.Pin_0
  N13: SM3.pin1, RELAY5.C
  N14: SM3.pin2, RELAY5.NC, RELAY6.NC, RELAY7.NO, IC2.pin5, C6.+
  N15: SM3.pin3, RELAY6.C
  N16: SM2.pin1, RELAY3.C
  N17: SM2.pin2, RELAY3.NC, RELAY4.NC
  N18: SM2.pin3, RELAY4.C
  N19: SM1.pin1, RELAY1.C
  N20: SM1.pin2, RELAY1.NC, RELAY2.NC
  N21: SM1.pin3, RELAY2.C
  N22: RELAY1.+, D1.A, Q1.C
  N23: RELAY1.-, D1.C, RELAY2.-, D2.C, RELAY3.-, D3.C, RELAY4.-, D4.C, RELAY5.-, D5.C, RELAY6.-, D6.C, RELAY7.-, D7.C, C5.+, IC2.pin1, PE52628NL.pin2, J1.pin2, Part1.VIN
  N24: OC2.pin1, 3_3K_4.Pin_1
  N25: OC2.pin3, 3_3K_3.Pin_1
  N26: OC2.pin6, 10K_4.Pin_1, Part1.D5
  N27: OC2.pin8, 10K_3.Pin_1, Part1.D4
  N28: OC3.pin1, 3_3K_6.Pin_1
  N29: OC3.pin3, 3_3K_5.Pin_1
  N30: OC3.pin6, 10K_6.Pin_1, Part1.D7
  N31: OC3.pin8, 10K_5.Pin_1, Part1.D6
  N32: QR1.Pin_0, Part1.A0
  N33: QR1.Pin_1, Q1.B
  N34: RELAY2.+, D2.A, Q2.C
  N35: QR2.Pin_0, Part1.A1
  N36: QR2.Pin_1, Q2.B
  N37: RELAY3.+, D3.A, Q3.C
  N38: QR3.Pin_0, Part1.A2
  N39: QR3.Pin_1, Q3.B
  N40: RELAY4.+, D4.A, Q4.C
  N41: QR4.Pin_0, Part1.A3
  N42: QR4.Pin_1, Q4.B
  N43: RELAY5.+, D5.A, Q5.C
  N44: QR5.Pin_0, Part1.A4
  N45: QR5.Pin_1, Q5.B
  N46: RELAY6.+, D6.A, Q6.C
  N47: QR6.Pin_0, Part1.A5
  N48: QR6.Pin_1, Q6.B
  N49: RELAY7.+, D7.A, Q7.C
  N50: QR7.Pin_0, Part1.A6
  N51: QR7.Pin_1, Q7.B
  N52: IC2.pin7, PE52628NL.pin1, D8.C
  N53: 10K.Pin_0, 10K_2.Pin_0, 10K_3.Pin_0, 10K_4.Pin_0, 10K_5.Pin_0, 10K_6.Pin_0, J1.pin1, Part1.3V3
  N54: J2.pin1, Part1.D1
  N55: J2.pin2, Part1.D0
  N56: J1.pin4, Part1.RX
  N57: J1.pin5, Part1.TX
  N58: J1.pin6, Part1.A7

notes:
  A7 TX RX GND
  SparkSofa
  D0 D1
  VIN 3V3

custom parts:
  Screw terminal - 4 pins: Screw terminal with 4 pins
  RELAY-SOLIDSTATE: SPST SS relay
  PE-52628N: PULSE ENGINEERING, PE-52628NL, INDUCTOR, 470UH, SMT, 0.9A, 11
